# Fritzing sketch Rotary DIP Switch (saved by Fritzing 0.6.3b)
breadboards: 1

parts:
  J1 = female pin header, 3 pins [form="♂ (male)"]
  J2 = female pin header, 3 pins [form="♂ (male)"]
  Netduino1 = Netduino

nets:
  N1: J1.pin1, Netduino1.D8_CTS1
  N2: J1.pin2, J2.pin2, Netduino1.GND
  N3: J1.pin3, Netduino1.D2_RX1
  N4: J2.pin1, Netduino1.D1_TX0
  N5: J2.pin3, Netduino1.D4_CS0
